// Logisim project 1-8demux_full_subtractor.circ as structural Verilog: 1 circuit, main circuit main
module main (
  input  in_1,
  input  [2:0] in_2,
  output out_3,
  output out_4,
  output out_5,
  output out_6,
  output out_7
);

  wire demultiplexer_1_out1, demultiplexer_1_out2, demultiplexer_1_out4, demultiplexer_1_out5,
       demultiplexer_1_out7;

  Demultiplexer #(.select(3), .width(1), .tristate("true")) demultiplexer_1 (
    .out0(out_3), .out1(demultiplexer_1_out1), .out2(demultiplexer_1_out2), .out3(out_5),
    .out4(demultiplexer_1_out4), .out5(demultiplexer_1_out5), .out6(out_6), .out7(demultiplexer_1_out7),
    .in(in_1), .sel(in_2));
  or or_1 (out_4, demultiplexer_1_out1, demultiplexer_1_out2, demultiplexer_1_out4, demultiplexer_1_out7);
  or or_2 (out_7, demultiplexer_1_out5, demultiplexer_1_out7, demultiplexer_1_out4, demultiplexer_1_out1);
endmodule
